// Logisim project cpu.circ as structural Verilog
module cpu (
);

  wire clk, half_mem, isIMM, memload, memstore, registerfile_1_p16, registerfile_1_p17, registerfile_1_p18,
       regwrite, RST;
  wire [1:0] regmux, regwritemux;
  wire [3:0] aluop;
  wire [4:0] multiplexer_2_out, rs_addr, rt_addr;
  wire [5:0] funcode, opcode;
  wire [15:0] \总周期数 , \无条件分支指令数 , \有条件分支成功跳转 , \有条件分支指令数 ;
  wire [15:6] imm16;
  wire [31:0] alu_out, bit_extender_1_out, bit_extender_2_out, bit_extender_3_out, mem_out, mips_ram_1_p7,
       multiplexer_1_out, multiplexer_3_out, PC_q, registerfile_1_p13, registerfile_1_p14, SyscallOut;

  Button \u_总复位  (.out(RST));
  Register #(.width(32)) PC (.Q(PC_q), .clk(clk));  // open: D, en, clr
  Clock clock_1 (.out(clk));
  Hex_Digit_Display hex_digit_display_1 (.value(SyscallOut[27:24]));  // open: dp
  Hex_Digit_Display hex_digit_display_2 (.value(SyscallOut[31:28]));  // open: dp
  Hex_Digit_Display hex_digit_display_3 (.value(SyscallOut[23:20]));  // open: dp
  Hex_Digit_Display hex_digit_display_4 (.value(SyscallOut[19:16]));  // open: dp
  Hex_Digit_Display hex_digit_display_5 (.value(SyscallOut[11:8]));  // open: dp
  Hex_Digit_Display hex_digit_display_6 (.value(SyscallOut[15:12]));  // open: dp
  ROM #(.addrWidth(24), .dataWidth(32)) rom_1 (
    .addr(PC_q[25:2]), .data({opcode, rs_addr, rt_addr, imm16, funcode}));  // open: sel
  Hex_Digit_Display hex_digit_display_7 (.value(SyscallOut[7:4]));  // open: dp
  Hex_Digit_Display hex_digit_display_8 (.value(SyscallOut[3:0]));  // open: dp
  assign bit_extender_1_out = {{16{imm16[15]}}, {imm16, funcode}};  // Bit_Extender bit_extender_1
  Multiplexer #(.select(2), .width(32), .disabled(0), .enable("false")) multiplexer_1 (
    .in0(alu_out), .in1(PC_q), .in2(mem_out), .out(multiplexer_1_out), .sel(regmux));  // open: in3
  // Probe on \总周期数 
  // Probe on \无条件分支指令数 
  // Probe on \有条件分支指令数 
  // Probe on \有条件分支成功跳转 
  Multiplexer #(.select(2), .width(5), .enable("false")) multiplexer_2 (
    .in0(imm16[15:11]), .in1(rt_addr), .in2({5{1'b1}}), .out(multiplexer_2_out), .sel(regwritemux));  // open: in3
  // RegisterFile registerfile_1: pin names not known; wires that end beside it: multiplexer_1_out, clk, regwrite, multiplexer_2_out, rs_addr, rt_addr, regwrite, isIMM, memstore, memload, half_mem, regwritemux, registerfile_1_p13, registerfile_1_p14, registerfile_1_p14, registerfile_1_p16, registerfile_1_p17, registerfile_1_p18
  Multiplexer #(.width(32), .enable("false")) multiplexer_3 (
    .in0(registerfile_1_p14), .in1(bit_extender_1_out), .out(multiplexer_3_out), .sel(isIMM));
  ALU alu_1 (
    .AluOP(aluop), .X(registerfile_1_p13), .Equal(registerfile_1_p18), .Result(alu_out),
    .Signed_Overflow(registerfile_1_p16), .Y(multiplexer_3_out), .UnSigned_Overflow(registerfile_1_p17),
    .shamt(imm16[10:6]));  // open: Result_2
  // MIPS_RAM mips_ram_1: pin names not known; wires that end beside it: alu_out[25:2], registerfile_1_p13, memstore, clk, memload, RST, mips_ram_1_p7
  assign bit_extender_2_out = {{16{1'b0}}, mips_ram_1_p7[15:0]};  // Bit_Extender bit_extender_2
  assign bit_extender_3_out = {{16{1'b0}}, mips_ram_1_p7[31:16]};  // Bit_Extender bit_extender_3
  Multiplexer #(.select(2), .width(32), .enable("false")) multiplexer_4 (
    .in0(mips_ram_1_p7), .in2(bit_extender_2_out), .in3(bit_extender_3_out), .out(mem_out),
    .sel({half_mem, alu_out[1]}));  // open: in1

  // Other names for the same wires on the sheet: imm16[5:0] = funcode; shamt[4:0] = imm16[10:6];
  //   rd_addr[4:0] = imm16[15:11]; HALF_SELECT = alu_out[1]

  // Notes on the sheet:
  //   数码管输出应该用寄存器锁存，否则显示数据只能一闪而过
  //   可以通过项目增加Logisim库的方式将前几次实验完成的电路作为子电路引入到本电路中使用
  //   数码管输出
  //   总复位信号应将除ROM以外所有存储组件全部清零
endmodule
